// Logisim project IPHOnE21-complete-project..circ as structural Verilog: 4 circuits, main circuit main
module main (
  input  in_1,
  input  in_2
);

  wire clock_1_out, combination_using_universal_gate_1_output_a, combination_using_universal_gate_1_output_b,
       combination_using_universal_gate_1_output_c, combination_using_universal_gate_1_output_d,
       combination_using_universal_gate_1_output_e, combination_using_universal_gate_1_output_f,
       combination_using_universal_gate_1_output_g, sequential_using_j_k_flipflop_1_output_0,
       sequential_using_j_k_flipflop_1_output_1, sequential_using_j_k_flipflop_1_output_2;

  Clock clock_1 (.out(clock_1_out));
  Sequential_using_j_k_flipflop sequential_using_j_k_flipflop_1 (
    .Enable(in_1), .Reset(in_2), .Output_2(sequential_using_j_k_flipflop_1_output_2),
    .Output_1(sequential_using_j_k_flipflop_1_output_1), .Output_0(sequential_using_j_k_flipflop_1_output_0),
    .Clock(clock_1_out));
  Combination_using_universal_gate combination_using_universal_gate_1 (
    .Output_A(combination_using_universal_gate_1_output_a),
    .Output_B(combination_using_universal_gate_1_output_b),
    .Output_C(combination_using_universal_gate_1_output_c),
    .Output_D(combination_using_universal_gate_1_output_d),
    .Output_E(combination_using_universal_gate_1_output_e),
    .Output_F(combination_using_universal_gate_1_output_f),
    .Output_G(combination_using_universal_gate_1_output_g),
    .Input_2(sequential_using_j_k_flipflop_1_output_2), .Input_1(sequential_using_j_k_flipflop_1_output_1),
    .Input_0(sequential_using_j_k_flipflop_1_output_0));
  _7_Segment_Display u_7_segment_display_1 (
    .g(combination_using_universal_gate_1_output_g), .f(combination_using_universal_gate_1_output_f),
    .a(combination_using_universal_gate_1_output_a), .b(combination_using_universal_gate_1_output_b),
    .e(combination_using_universal_gate_1_output_e), .d(combination_using_universal_gate_1_output_d),
    .c(combination_using_universal_gate_1_output_c));  // open: dp
endmodule

module Combination_using_universal_gate (
  input  Input_2,
  input  Input_1,
  input  Input_0,
  output Output_A,
  output Output_B,
  output Output_C,
  output Output_D,
  output Output_E,
  output Output_F,
  output Output_G
);

  wire nand_1_out, nand_2_out, nand_3_out, nand_4_out, nand_5_out, nand_6_out, nand_7_out, nand_8_out,
       nand_9_out, nand_10_out, nand_11_out, nand_12_out, nand_13_out, nand_14_out, nand_15_out, nand_16_out,
       nand_17_out, nand_18_out, nand_19_out, nand_20_out;

  nand nand_1 (nand_1_out, Input_2, Input_2);
  nand nand_2 (nand_2_out, Input_1, Input_1);
  nand nand_3 (nand_3_out, Input_0, Input_0);
  nand nand_4 (nand_4_out, nand_1_out, Input_0);
  nand nand_5 (nand_5_out, nand_2_out, Input_0);
  nand nand_6 (nand_6_out, Input_2, Input_1, nand_3_out);
  nand nand_7 (nand_7_out, nand_2_out, nand_3_out);
  nand nand_8 (nand_8_out, nand_1_out, Input_1);
  nand nand_9 (nand_9_out, Input_1, Input_0);
  nand nand_10 (nand_10_out, Input_2, nand_2_out, Input_0);
  nand nand_11 (nand_11_out, nand_1_out, Input_1, Input_0);
  nand nand_12 (nand_12_out, Input_2, Input_1, nand_3_out);
  nand nand_13 (nand_13_out, nand_1_out, Input_0);
  nand nand_14 (nand_14_out, Input_1, nand_3_out);
  nand nand_15 (nand_15_out, Input_2, nand_2_out);
  nand nand_16 (nand_16_out, nand_2_out, Input_0);
  nand nand_17 (nand_17_out, nand_1_out, Input_1);
  nand nand_18 (nand_18_out, Input_2, nand_2_out);
  nand nand_19 (nand_19_out, nand_2_out, Input_0);
  nand nand_20 (nand_20_out, Input_1, nand_3_out);
  nand nand_21 (Output_A, nand_4_out, nand_5_out, nand_6_out);
  nand nand_22 (Output_B, Input_2, nand_2_out);
  nand nand_23 (Output_C, nand_7_out, nand_8_out, nand_9_out);
  nand nand_24 (Output_D, nand_10_out, nand_11_out, nand_12_out);
  nand nand_25 (Output_E, nand_13_out, nand_14_out, nand_15_out);
  nand nand_26 (Output_F, nand_16_out, nand_17_out);
  nand nand_27 (Output_G, nand_18_out, nand_19_out, nand_20_out);
endmodule

module Combination_using_basic_gate (
  input  in_1,
  input  in_2,
  input  in_3
);

  wire and_1_out, and_2_out, and_3_out, and_4_out, and_5_out, and_6_out, and_7_out, and_8_out, and_9_out,
       and_10_out, and_11_out, and_12_out, and_13_out, and_14_out, and_15_out, and_16_out, and_17_out,
       not_1_out, not_2_out, not_3_out, or_1_out, or_2_out, or_3_out, or_4_out, or_5_out, or_6_out, or_7_out;

  not not_1 (not_1_out, in_1);
  not not_2 (not_2_out, in_2);
  not not_3 (not_3_out, in_3);
  and and_1 (and_1_out, not_1_out, in_3);
  and and_2 (and_2_out, not_2_out, in_3);
  and and_3 (and_3_out, in_1, in_2, not_3_out);
  and and_4 (and_4_out, not_2_out, not_3_out);
  and and_5 (and_5_out, not_1_out, in_2);
  and and_6 (and_6_out, in_2, in_3);
  and and_7 (and_7_out, in_1, not_2_out, in_3);
  and and_8 (and_8_out, not_1_out, in_2, in_3);
  and and_9 (and_9_out, in_1, in_2, not_3_out);
  and and_10 (and_10_out, not_1_out, in_3);
  and and_11 (and_11_out, in_2, not_3_out);
  and and_12 (and_12_out, in_1, not_2_out);
  and and_13 (and_13_out, not_2_out, in_3);
  and and_14 (and_14_out, not_1_out, in_2);
  and and_15 (and_15_out, in_1, not_2_out);
  and and_16 (and_16_out, not_2_out, in_3);
  and and_17 (and_17_out, in_2, not_3_out);
  or or_1 (or_1_out, and_1_out, and_2_out, and_3_out);
  or or_2 (or_2_out, not_1_out, in_2);
  or or_3 (or_3_out, and_4_out, and_5_out, and_6_out);
  or or_4 (or_4_out, and_7_out, and_8_out, and_9_out);
  or or_5 (or_5_out, and_10_out, and_11_out, and_12_out);
  or or_6 (or_6_out, and_13_out, and_14_out);
  or or_7 (or_7_out, and_15_out, and_16_out, and_17_out);
  _7_Segment_Display u_7_segment_display_1 (
    .g(or_7_out), .f(or_6_out), .a(or_1_out), .b(or_2_out), .e(or_5_out), .d(or_4_out), .c(or_3_out));  // open: dp
endmodule

module Sequential_using_j_k_flipflop (
  input  Clock,
  input  Enable,
  input  Reset,
  output Output_2,
  output Output_1,
  output Output_0
);

  wire and_1_out;

  and and_1 (and_1_out, Output_0, Output_1);
  J_K_Flip_Flop j_k_flipflop_2 (
    .J(and_1_out), .clk(Clock), .K(and_1_out), .Q(Output_2), .en(Enable), .reset(Reset));  // open: Qn, preset
  J_K_Flip_Flop j_k_flipflop_1 (
    .J(Output_0), .clk(Clock), .K(Output_0), .Q(Output_1), .en(Enable), .reset(Reset));  // open: Qn, preset
  J_K_Flip_Flop j_k_flipflop_0 (
    .J(1'b1), .clk(Clock), .K(1'b1), .Q(Output_0), .en(Enable), .reset(Reset));  // open: Qn, preset
endmodule
