// Logisim project IPHOnE21_project_complete.circ as structural Verilog
module _7400 (
  input  Vcc,
  input  _1A,
  input  _1B,
  input  _2A,
  input  _2B,
  input  _3A,
  input  _3B,
  input  _4A,
  input  _4B,
  input  GND,
  output _1Y,
  output _2Y,
  output _3Y,
  output _4Y
);

  nand nand_1 (_1Y, _1A, _1B);
  nand nand_2 (_2Y, _2A, _2B);
  nand nand_3 (_3Y, _3A, _3B);
  nand nand_4 (_4Y, _4A, _4B);
endmodule

module _7408 (
  input  Vcc,
  input  _1A,
  input  _1B,
  input  _2A,
  input  _2B,
  input  _3A,
  input  _3B,
  input  _4A,
  input  _4B,
  input  GND,
  output _1Y,
  output _2Y,
  output _3Y,
  output _4Y
);

  and and_1 (_1Y, _1A, _1B);
  and and_2 (_2Y, _2A, _2B);
  and and_3 (_3Y, _3A, _3B);
  and and_4 (_4Y, _4A, _4B);
endmodule

module _7410 (
  input  Vcc,
  input  _1A,
  input  _1B,
  input  _1C,
  input  _2A,
  input  _2B,
  input  _2C,
  input  _3A,
  input  _3B,
  input  _3C,
  input  GND,
  output _1Y,
  output _2Y,
  output _3Y
);

  nand nand_1 (_1Y, _1A, _1B, _1C);
  nand nand_2 (_2Y, _2A, _2B, _2C);
  nand nand_3 (_3Y, _3A, _3B, _3C);
endmodule

module _7473 (
  input  Vcc,
  input  J1,
  input  K1,
  input  CLK1,
  input  CLR1,
  input  J2,
  input  K2,
  input  CLK2,
  input  CLR2,
  input  GND,
  output Q1,
  output Q1_prime,
  output Q2,
  output Q2_prime
);

  wire and_1_out, and_2_out, and_3_out, and_4_out, and_5_out, and_6_out, and_7_out, and_8_out, nor_1_out,
       nor_2_out, nor_3_out, nor_4_out, not_1_out, not_2_out;

  and and_1 (and_1_out, Q1_prime, J1, CLK1);
  and and_2 (and_2_out, CLK1, K1, Q1);
  not not_1 (not_1_out, CLK1);
  and and_3 (and_3_out, Q2_prime, J2, CLK2);
  and and_4 (and_4_out, CLK2, K2, Q2);
  not not_2 (not_2_out, CLK2);
  nor nor_1 (nor_1_out, and_1_out, nor_2_out);
  nor nor_2 (nor_2_out, nor_1_out, and_2_out, CLR1);
  nor nor_3 (nor_3_out, and_3_out, nor_4_out);
  nor nor_4 (nor_4_out, nor_3_out, and_4_out, CLR2);
  and and_5 (and_5_out, not_1_out, nor_1_out);
  nor nor_5 (Q1, and_5_out, Q1_prime);
  nor nor_6 (Q1_prime, Q1, and_6_out);
  and and_6 (and_6_out, nor_2_out, not_1_out);
  and and_7 (and_7_out, not_2_out, nor_3_out);
  nor nor_7 (Q2, and_7_out, Q2_prime);
  nor nor_8 (Q2_prime, Q2, and_8_out);
  and and_8 (and_8_out, nor_4_out, not_2_out);
endmodule

module Combinational_part_using_basic_gate (
  input  in_1,
  input  in_2,
  input  in_3
);

  wire and_1_out, and_2_out, and_3_out, and_4_out, and_5_out, and_6_out, and_7_out, and_8_out, and_9_out,
       and_10_out, and_11_out, and_12_out, and_13_out, and_14_out, and_15_out, and_16_out, and_17_out,
       not_1_out, not_2_out, not_3_out, or_1_out, or_2_out, or_3_out, or_4_out, or_5_out, or_6_out, or_7_out;

  not not_1 (not_1_out, in_1);
  not not_2 (not_2_out, in_2);
  not not_3 (not_3_out, in_3);
  and and_1 (and_1_out, not_1_out, in_3);
  and and_2 (and_2_out, not_2_out, in_3);
  and and_3 (and_3_out, in_1, in_2, not_3_out);
  and and_4 (and_4_out, not_2_out, not_3_out);
  and and_5 (and_5_out, not_1_out, in_2);
  and and_6 (and_6_out, in_2, in_3);
  and and_7 (and_7_out, in_1, not_2_out, in_3);
  and and_8 (and_8_out, not_1_out, in_2, in_3);
  and and_9 (and_9_out, in_1, in_2, not_3_out);
  and and_10 (and_10_out, not_1_out, in_3);
  and and_11 (and_11_out, in_2, not_3_out);
  and and_12 (and_12_out, in_1, not_2_out);
  and and_13 (and_13_out, not_2_out, in_3);
  and and_14 (and_14_out, not_1_out, in_2);
  and and_15 (and_15_out, in_1, not_2_out);
  and and_16 (and_16_out, not_2_out, in_3);
  and and_17 (and_17_out, in_2, not_3_out);
  or or_1 (or_1_out, and_1_out, and_2_out, and_3_out);
  or or_2 (or_2_out, not_1_out, in_2);
  or or_3 (or_3_out, and_4_out, and_5_out, and_6_out);
  or or_4 (or_4_out, and_7_out, and_8_out, and_9_out);
  or or_5 (or_5_out, and_10_out, and_11_out, and_12_out);
  or or_6 (or_6_out, and_13_out, and_14_out);
  or or_7 (or_7_out, and_15_out, and_16_out, and_17_out);
  _7_Segment_Display u_7_segment_display_1 (
    .g(or_7_out), .f(or_6_out), .a(or_1_out), .b(or_2_out), .e(or_5_out), .d(or_4_out), .c(or_3_out));  // open: dp
endmodule

module Combinational_part_using_universal_gate_NAND_GATE (
  input  Input_2,
  input  Input_1,
  input  Input_0,
  output Output_A,
  output Output_B,
  output Output_C,
  output Output_D,
  output Output_E,
  output Output_F,
  output Output_G
);

  wire nand_1_out, nand_2_out, nand_3_out, nand_4_out, nand_5_out, nand_6_out, nand_7_out, nand_8_out,
       nand_9_out, nand_10_out, nand_11_out, nand_12_out, nand_13_out, nand_14_out, nand_15_out, nand_16_out,
       nand_17_out, nand_18_out, nand_19_out, nand_20_out;

  nand nand_1 (nand_1_out, Input_2, Input_2);
  nand nand_2 (nand_2_out, Input_1, Input_1);
  nand nand_3 (nand_3_out, Input_0, Input_0);
  nand nand_4 (nand_4_out, nand_1_out, Input_0);
  nand nand_5 (nand_5_out, nand_2_out, Input_0);
  nand nand_6 (nand_6_out, Input_2, Input_1, nand_3_out);
  nand nand_7 (nand_7_out, nand_2_out, nand_3_out);
  nand nand_8 (nand_8_out, nand_1_out, Input_1);
  nand nand_9 (nand_9_out, Input_1, Input_0);
  nand nand_10 (nand_10_out, Input_2, nand_2_out, Input_0);
  nand nand_11 (nand_11_out, nand_1_out, Input_1, Input_0);
  nand nand_12 (nand_12_out, Input_2, Input_1, nand_3_out);
  nand nand_13 (nand_13_out, nand_1_out, Input_0);
  nand nand_14 (nand_14_out, Input_1, nand_3_out);
  nand nand_15 (nand_15_out, Input_2, nand_2_out);
  nand nand_16 (nand_16_out, nand_2_out, Input_0);
  nand nand_17 (nand_17_out, nand_1_out, Input_1);
  nand nand_18 (nand_18_out, Input_2, nand_2_out);
  nand nand_19 (nand_19_out, nand_2_out, Input_0);
  nand nand_20 (nand_20_out, Input_1, nand_3_out);
  nand nand_21 (Output_A, nand_4_out, nand_5_out, nand_6_out);
  nand nand_22 (Output_B, Input_2, nand_2_out);
  nand nand_23 (Output_C, nand_7_out, nand_8_out, nand_9_out);
  nand nand_24 (Output_D, nand_10_out, nand_11_out, nand_12_out);
  nand nand_25 (Output_E, nand_13_out, nand_14_out, nand_15_out);
  nand nand_26 (Output_F, nand_16_out, nand_17_out);
  nand nand_27 (Output_G, nand_18_out, nand_19_out, nand_20_out);
endmodule

module Sequential_part_using_J_K_flipflop (
  input  Clock,
  input  Enable,
  input  Reset,
  output Output_2,
  output Output_1,
  output Output_0
);

  wire and_1_out;

  and and_1 (and_1_out, Output_0, Output_1);
  J_K_Flip_Flop j_k_flipflop_2 (
    .J(and_1_out), .clk(Clock), .K(and_1_out), .Q(Output_2), .en(Enable), .reset(Reset));  // open: Qn, preset
  J_K_Flip_Flop j_k_flipflop_1 (
    .J(Output_0), .clk(Clock), .K(Output_0), .Q(Output_1), .en(Enable), .reset(Reset));  // open: Qn, preset
  J_K_Flip_Flop j_k_flipflop_0 (
    .J(1'b1), .clk(Clock), .K(1'b1), .Q(Output_0), .en(Enable), .reset(Reset));  // open: Qn, preset
endmodule

module Sequential_part_and_Combinational_part_Universal_gate (
  input  Enable,
  input  Reset
);

  wire and_1_out, Clock_out, j_k_flipflop_0_q, j_k_flipflop_1_q, j_k_flipflop_2_q, nand_1_out, nand_2_out,
       nand_3_out, nand_4_out, nand_5_out, nand_6_out, nand_7_out, nand_8_out, nand_9_out, nand_10_out,
       nand_11_out, nand_12_out, nand_13_out, nand_14_out, nand_15_out, nand_16_out, nand_17_out,
       nand_18_out, nand_19_out, nand_20_out, nand_21_out, nand_22_out, nand_23_out, nand_24_out,
       nand_25_out, nand_26_out, nand_27_out;

  Clock Clock (.out(Clock_out));
  and and_1 (and_1_out, j_k_flipflop_0_q, j_k_flipflop_1_q);
  J_K_Flip_Flop j_k_flipflop_2 (
    .J(and_1_out), .clk(Clock_out), .K(and_1_out), .Q(j_k_flipflop_2_q), .en(Enable), .reset(Reset));  // open: Qn, preset
  J_K_Flip_Flop j_k_flipflop_1 (
    .J(j_k_flipflop_0_q), .clk(Clock_out), .K(j_k_flipflop_0_q), .Q(j_k_flipflop_1_q), .en(Enable),
    .reset(Reset));  // open: Qn, preset
  J_K_Flip_Flop j_k_flipflop_0 (
    .J(1'b1), .clk(Clock_out), .K(1'b1), .Q(j_k_flipflop_0_q), .en(Enable), .reset(Reset));  // open: Qn, preset
  nand nand_1 (nand_1_out, j_k_flipflop_2_q, j_k_flipflop_2_q);
  nand nand_2 (nand_2_out, j_k_flipflop_1_q, j_k_flipflop_1_q);
  nand nand_3 (nand_3_out, j_k_flipflop_0_q, j_k_flipflop_0_q);
  nand nand_4 (nand_4_out, nand_1_out, j_k_flipflop_0_q);
  nand nand_5 (nand_5_out, nand_2_out, j_k_flipflop_0_q);
  nand nand_6 (nand_6_out, j_k_flipflop_2_q, j_k_flipflop_1_q, nand_3_out);
  nand nand_7 (nand_7_out, nand_2_out, nand_3_out);
  nand nand_8 (nand_8_out, nand_1_out, j_k_flipflop_1_q);
  nand nand_9 (nand_9_out, j_k_flipflop_1_q, j_k_flipflop_0_q);
  nand nand_10 (nand_10_out, j_k_flipflop_2_q, nand_2_out, j_k_flipflop_0_q);
  nand nand_11 (nand_11_out, nand_1_out, j_k_flipflop_1_q, j_k_flipflop_0_q);
  nand nand_12 (nand_12_out, j_k_flipflop_2_q, j_k_flipflop_1_q, nand_3_out);
  nand nand_13 (nand_13_out, nand_1_out, j_k_flipflop_0_q);
  nand nand_14 (nand_14_out, j_k_flipflop_1_q, nand_3_out);
  nand nand_15 (nand_15_out, j_k_flipflop_2_q, nand_2_out);
  nand nand_16 (nand_16_out, nand_2_out, j_k_flipflop_0_q);
  nand nand_17 (nand_17_out, nand_1_out, j_k_flipflop_1_q);
  nand nand_18 (nand_18_out, j_k_flipflop_2_q, nand_2_out);
  nand nand_19 (nand_19_out, nand_2_out, j_k_flipflop_0_q);
  nand nand_20 (nand_20_out, j_k_flipflop_1_q, nand_3_out);
  nand nand_21 (nand_21_out, nand_4_out, nand_5_out, nand_6_out);
  nand nand_22 (nand_22_out, j_k_flipflop_2_q, nand_2_out);
  nand nand_23 (nand_23_out, nand_7_out, nand_8_out, nand_9_out);
  nand nand_24 (nand_24_out, nand_10_out, nand_11_out, nand_12_out);
  nand nand_25 (nand_25_out, nand_13_out, nand_14_out, nand_15_out);
  nand nand_26 (nand_26_out, nand_16_out, nand_17_out);
  nand nand_27 (nand_27_out, nand_18_out, nand_19_out, nand_20_out);
  _7_Segment_Display u_7_segment_display_1 (
    .g(nand_27_out), .f(nand_26_out), .a(nand_21_out), .b(nand_22_out), .e(nand_25_out), .d(nand_24_out),
    .c(nand_23_out));  // open: dp
endmodule

module Sequential_part_and_Combinational_part_Universal_gate__using_custom_ic (
  input  in_1,
  input  in_2
);

  wire clock_1_out, combinational_part_using_universal_gate_nand_gate_1_output_a,
       combinational_part_using_universal_gate_nand_gate_1_output_b,
       combinational_part_using_universal_gate_nand_gate_1_output_c,
       combinational_part_using_universal_gate_nand_gate_1_output_d,
       combinational_part_using_universal_gate_nand_gate_1_output_e,
       combinational_part_using_universal_gate_nand_gate_1_output_f,
       combinational_part_using_universal_gate_nand_gate_1_output_g,
       sequential_part_using_j_k_flipflop_1_output_0, sequential_part_using_j_k_flipflop_1_output_1,
       sequential_part_using_j_k_flipflop_1_output_2;

  Clock clock_1 (.out(clock_1_out));
  Sequential_part_using_J_K_flipflop sequential_part_using_j_k_flipflop_1 (
    .Clock(clock_1_out), .Enable(in_1), .Reset(in_2),
    .Output_2(sequential_part_using_j_k_flipflop_1_output_2),
    .Output_1(sequential_part_using_j_k_flipflop_1_output_1),
    .Output_0(sequential_part_using_j_k_flipflop_1_output_0));
  Combinational_part_using_universal_gate_NAND_GATE combinational_part_using_universal_gate_nand_gate_1 (
    .Output_A(combinational_part_using_universal_gate_nand_gate_1_output_a),
    .Output_B(combinational_part_using_universal_gate_nand_gate_1_output_b),
    .Output_C(combinational_part_using_universal_gate_nand_gate_1_output_c),
    .Output_D(combinational_part_using_universal_gate_nand_gate_1_output_d),
    .Output_E(combinational_part_using_universal_gate_nand_gate_1_output_e),
    .Output_F(combinational_part_using_universal_gate_nand_gate_1_output_f),
    .Output_G(combinational_part_using_universal_gate_nand_gate_1_output_g),
    .Input_2(sequential_part_using_j_k_flipflop_1_output_2),
    .Input_1(sequential_part_using_j_k_flipflop_1_output_1),
    .Input_0(sequential_part_using_j_k_flipflop_1_output_0));
  _7_Segment_Display u_7_segment_display_1 (
    .g(combinational_part_using_universal_gate_nand_gate_1_output_g),
    .f(combinational_part_using_universal_gate_nand_gate_1_output_f),
    .a(combinational_part_using_universal_gate_nand_gate_1_output_a),
    .b(combinational_part_using_universal_gate_nand_gate_1_output_b),
    .e(combinational_part_using_universal_gate_nand_gate_1_output_e),
    .d(combinational_part_using_universal_gate_nand_gate_1_output_d),
    .c(combinational_part_using_universal_gate_nand_gate_1_output_c));  // open: dp
endmodule

module Combinational_part_using_NAND_IC_7400__7410 (
  input  Input_2,
  input  Input_1,
  input  Input_0,
  output Output_A,
  output Output_B,
  output Output_C,
  output Output_D,
  output Output_E,
  output Output_F,
  output Output_G
);

  wire n7400_1__1y, n7400_1__2y, n7400_1__4y, n7400_2__1y, n7400_2__2y, n7400_2__3y, n7400_2__4y,
       n7400_3__2y, n7400_3__4y, n7410_1__1y, n7410_1__2y, n7410_1__3y;

  _7400 u_7400_1 (
    .Vcc(1'b1), ._1A(Input_0), ._1B(Input_0), ._2A(Input_1), ._2B(Input_1), ._4A(Input_2), ._4B(Input_2),
    .GND(1'b0), ._1Y(n7400_1__1y), ._2Y(n7400_1__2y), ._4Y(n7400_1__4y));  // open: _3A, _3B, _3Y
  _7400 u_7400_2 (
    .Vcc(1'b1), ._1A(n7400_1__4y), ._1B(Input_1), ._2A(n7400_1__4y), ._2B(Input_0), ._3A(Input_0),
    ._3B(n7400_1__2y), ._4A(n7400_1__1y), ._4B(Input_1), .GND(1'b0), ._1Y(n7400_2__1y), ._2Y(n7400_2__2y),
    ._3Y(n7400_2__3y), ._4Y(n7400_2__4y));
  _7400 u_7400_3 (
    .Vcc(1'b1), ._1A(Input_2), ._1B(n7400_1__2y), ._2A(Input_1), ._2B(Input_0), ._3A(n7400_2__3y),
    ._3B(n7400_2__1y), ._4A(n7400_1__1y), ._4B(n7400_1__2y), .GND(1'b0), ._1Y(Output_B), ._2Y(n7400_3__2y),
    ._3Y(Output_F), ._4Y(n7400_3__4y));
  _7410 u_7410_1 (
    .Vcc(1'b1), ._1A(Input_2), ._1B(Input_1), ._1C(n7400_1__1y), ._2A(n7400_1__4y), ._2B(Input_1),
    ._2C(Input_0), ._3A(Input_2), ._3B(n7400_1__2y), ._3C(Input_0), .GND(1'b0), ._1Y(n7410_1__1y),
    ._2Y(n7410_1__2y), ._3Y(n7410_1__3y));
  _7410 u_7410_2 (
    .Vcc(1'b1), ._1A(n7400_2__2y), ._1B(n7400_2__3y), ._1C(n7410_1__1y), ._2A(n7400_3__4y),
    ._2B(n7400_2__1y), ._2C(n7400_3__2y), ._3A(n7410_1__3y), ._3B(n7410_1__2y), ._3C(n7410_1__1y),
    .GND(1'b0), ._1Y(Output_A), ._2Y(Output_C), ._3Y(Output_D));
  _7410 u_7410_3 (
    .Vcc(1'b1), ._1A(n7400_2__2y), ._1B(n7400_2__4y), ._1C(Output_B), ._2A(n7400_2__4y), ._2B(Output_B),
    ._2C(n7400_2__3y), .GND(1'b0), ._1Y(Output_E), ._2Y(Output_G));  // open: _3A, _3B, _3C, _3Y
  _7_Segment_Display u_7_segment_display_1 (
    .g(Output_G), .f(Output_F), .a(Output_A), .b(Output_B), .e(Output_E), .d(Output_D), .c(Output_C));  // open: dp
endmodule

module Sequential_part_using_J_K_flipflop_IC_7473 (
  input  Clock,
  input  Clear,
  output out_3,
  output out_4,
  output out_5
);

  wire n7408_1__1y;

  _7408 u_7408_1 (
    ._1A(out_5), ._1B(out_4), ._1Y(n7408_1__1y));  // open: Vcc, _2A, _2B, _3A, _3B, _4A, _4B, GND, _2Y, _3Y, _4Y
  _7473 u_7473_1 (
    .J1(n7408_1__1y), .K1(n7408_1__1y), .CLK1(Clock), .CLR1(Clear), .J2(out_5), .K2(out_5), .CLK2(Clock),
    .CLR2(Clear), .Q1(out_3), .Q2(out_4), .Vcc(1'b1), .GND(1'b0));  // open: Q1_prime, Q2_prime
  _7473 u_7473_2 (
    .J1(1'b1), .K1(1'b1), .CLK1(Clock), .CLR1(Clear), .Q1(out_5), .Vcc(1'b1), .GND(1'b0));  // open: J2, K2, CLK2, CLR2, Q1_prime, Q2, Q2_prime
endmodule

module Sequential_part_IC__and_Combinational_part_IC (
  input  Clock,
  input  Clear
);

  wire n7400_1__1y, n7400_1__2y, n7400_1__4y, n7400_2__1y, n7400_2__2y, n7400_2__3y, n7400_2__4y,
       n7400_3__1y, n7400_3__2y, n7400_3__3y, n7400_3__4y, n7408_1__1y, n7410_1__1y, n7410_1__2y,
       n7410_1__3y, n7410_2__1y, n7410_2__2y, n7410_2__3y, n7410_3__1y, n7410_3__2y, n7473_1_q1, n7473_1_q2,
       n7473_2_q1;

  _7408 u_7408_1 (
    ._1A(n7473_2_q1), ._1B(n7473_1_q2), ._1Y(n7408_1__1y));  // open: Vcc, _2A, _2B, _3A, _3B, _4A, _4B, GND, _2Y, _3Y, _4Y
  _7473 u_7473_1 (
    .J1(n7408_1__1y), .K1(n7408_1__1y), .CLK1(Clock), .CLR1(Clear), .J2(n7473_2_q1), .K2(n7473_2_q1),
    .CLK2(Clock), .CLR2(Clear), .Q1(n7473_1_q1), .Q2(n7473_1_q2), .Vcc(1'b1), .GND(1'b0));  // open: Q1_prime, Q2_prime
  _7473 u_7473_2 (
    .J1(1'b1), .K1(1'b1), .CLK1(Clock), .CLR1(Clear), .Q1(n7473_2_q1), .Vcc(1'b1), .GND(1'b0));  // open: J2, K2, CLK2, CLR2, Q1_prime, Q2, Q2_prime
  _7400 u_7400_1 (
    .Vcc(1'b1), ._1A(n7473_2_q1), ._1B(n7473_2_q1), ._2A(n7473_1_q2), ._2B(n7473_1_q2), ._4A(n7473_1_q1),
    ._4B(n7473_1_q1), .GND(1'b0), ._1Y(n7400_1__1y), ._2Y(n7400_1__2y), ._4Y(n7400_1__4y));  // open: _3A, _3B, _3Y
  _7400 u_7400_2 (
    .Vcc(1'b1), ._1A(n7400_1__4y), ._1B(n7473_1_q2), ._2A(n7400_1__4y), ._2B(n7473_2_q1), ._3A(n7473_2_q1),
    ._3B(n7400_1__2y), ._4A(n7400_1__1y), ._4B(n7473_1_q2), .GND(1'b0), ._1Y(n7400_2__1y), ._2Y(n7400_2__2y),
    ._3Y(n7400_2__3y), ._4Y(n7400_2__4y));
  _7400 u_7400_3 (
    .Vcc(1'b1), ._1A(n7473_1_q1), ._1B(n7400_1__2y), ._2A(n7473_1_q2), ._2B(n7473_2_q1), ._3A(n7400_2__3y),
    ._3B(n7400_2__1y), ._4A(n7400_1__1y), ._4B(n7400_1__2y), .GND(1'b0), ._1Y(n7400_3__1y),
    ._2Y(n7400_3__2y), ._3Y(n7400_3__3y), ._4Y(n7400_3__4y));
  _7410 u_7410_1 (
    .Vcc(1'b1), ._1A(n7473_1_q1), ._1B(n7473_1_q2), ._1C(n7400_1__1y), ._2A(n7400_1__4y), ._2B(n7473_1_q2),
    ._2C(n7473_2_q1), ._3A(n7473_1_q1), ._3B(n7400_1__2y), ._3C(n7473_2_q1), .GND(1'b0), ._1Y(n7410_1__1y),
    ._2Y(n7410_1__2y), ._3Y(n7410_1__3y));
  _7410 u_7410_2 (
    .Vcc(1'b1), ._1A(n7400_2__2y), ._1B(n7400_2__3y), ._1C(n7410_1__1y), ._2A(n7400_3__4y),
    ._2B(n7400_2__1y), ._2C(n7400_3__2y), ._3A(n7410_1__3y), ._3B(n7410_1__2y), ._3C(n7410_1__1y),
    .GND(1'b0), ._1Y(n7410_2__1y), ._2Y(n7410_2__2y), ._3Y(n7410_2__3y));
  _7410 u_7410_3 (
    .Vcc(1'b1), ._1A(n7400_2__2y), ._1B(n7400_2__4y), ._1C(n7400_3__1y), ._2A(n7400_2__4y),
    ._2B(n7400_3__1y), ._2C(n7400_2__3y), .GND(1'b0), ._1Y(n7410_3__1y), ._2Y(n7410_3__2y));  // open: _3A, _3B, _3C, _3Y
  _7_Segment_Display u_7_segment_display_1 (
    .g(n7410_3__2y), .f(n7400_3__3y), .a(n7410_2__1y), .b(n7400_3__1y), .e(n7410_3__1y), .d(n7410_2__3y),
    .c(n7410_2__2y));  // open: dp
endmodule

module Sequential_part_IC__and_Combinational_part_IC__using_custom_ic (
  input  in_1
);

  wire clock_1_out, combinational_part_using_nand_ic_7400_7410_1_output_a,
       combinational_part_using_nand_ic_7400_7410_1_output_b,
       combinational_part_using_nand_ic_7400_7410_1_output_c,
       combinational_part_using_nand_ic_7400_7410_1_output_d,
       combinational_part_using_nand_ic_7400_7410_1_output_e,
       combinational_part_using_nand_ic_7400_7410_1_output_f,
       combinational_part_using_nand_ic_7400_7410_1_output_g,
       sequential_part_using_j_k_flipflop_ic_7473_1_out_3,
       sequential_part_using_j_k_flipflop_ic_7473_1_out_4, sequential_part_using_j_k_flipflop_ic_7473_1_out_5;

  Clock clock_1 (.out(clock_1_out));
  Sequential_part_using_J_K_flipflop_IC_7473 sequential_part_using_j_k_flipflop_ic_7473_1 (
    .Clock(clock_1_out), .Clear(in_1), .out_3(sequential_part_using_j_k_flipflop_ic_7473_1_out_3),
    .out_4(sequential_part_using_j_k_flipflop_ic_7473_1_out_4),
    .out_5(sequential_part_using_j_k_flipflop_ic_7473_1_out_5));
  Combinational_part_using_NAND_IC_7400__7410 combinational_part_using_nand_ic_7400_7410_1 (
    .Output_A(combinational_part_using_nand_ic_7400_7410_1_output_a),
    .Output_B(combinational_part_using_nand_ic_7400_7410_1_output_b),
    .Output_C(combinational_part_using_nand_ic_7400_7410_1_output_c),
    .Output_D(combinational_part_using_nand_ic_7400_7410_1_output_d),
    .Output_E(combinational_part_using_nand_ic_7400_7410_1_output_e),
    .Output_F(combinational_part_using_nand_ic_7400_7410_1_output_f),
    .Output_G(combinational_part_using_nand_ic_7400_7410_1_output_g),
    .Input_2(sequential_part_using_j_k_flipflop_ic_7473_1_out_3),
    .Input_1(sequential_part_using_j_k_flipflop_ic_7473_1_out_4),
    .Input_0(sequential_part_using_j_k_flipflop_ic_7473_1_out_5));
  _7_Segment_Display u_7_segment_display_1 (
    .g(combinational_part_using_nand_ic_7400_7410_1_output_g),
    .f(combinational_part_using_nand_ic_7400_7410_1_output_f),
    .a(combinational_part_using_nand_ic_7400_7410_1_output_a),
    .b(combinational_part_using_nand_ic_7400_7410_1_output_b),
    .e(combinational_part_using_nand_ic_7400_7410_1_output_e),
    .d(combinational_part_using_nand_ic_7400_7410_1_output_d),
    .c(combinational_part_using_nand_ic_7400_7410_1_output_c));  // open: dp
endmodule
