// Logisim project IPHOne21-Sequential-using-j-k-flipflop.circ as structural Verilog: 1 circuit, main circuit main
module main (
  input  Enable,
  input  Reset,
  output Output_2,
  output Output_1,
  output Output_0
);

  wire and_1_out, Clock_out;

  Clock Clock (.out(Clock_out));
  and and_1 (and_1_out, Output_0, Output_1);
  J_K_Flip_Flop j_k_flipflop_2 (
    .J(and_1_out), .clk(Clock_out), .K(and_1_out), .Q(Output_2), .en(Enable), .reset(Reset));  // open: Qn, preset
  J_K_Flip_Flop j_k_flipflop_1 (
    .J(Output_0), .clk(Clock_out), .K(Output_0), .Q(Output_1), .en(Enable), .reset(Reset));  // open: Qn, preset
  J_K_Flip_Flop j_k_flipflop_0 (
    .J(1'b1), .clk(Clock_out), .K(1'b1), .Q(Output_0), .en(Enable), .reset(Reset));  // open: Qn, preset
endmodule
